// Logisim project vergleicher.circ as structural Verilog: 1 circuit, main circuit main
module main (
);

  wire A_out, and_1_out, and_2_out, and_3_out, and_4_out, and_5_out, and_6_out, and_7_out, B_out, C_out,
       D_out, or_1_out, or_2_out;

  Button B (.out(B_out));
  Button A (.out(A_out));
  Button D (.out(D_out));
  Button C (.out(C_out));
  and and_1 (and_1_out, A_out, ~C_out);  // AND_Gate
  and and_2 (and_2_out, A_out, B_out, ~D_out, 1'b1);  // AND_Gate
  and and_3 (and_3_out, B_out, ~C_out, ~D_out, 1'b1);  // AND_Gate
  and and_4 (and_4_out, ~A_out, C_out);  // AND_Gate
  and and_5 (and_5_out, ~A_out, ~B_out, D_out, 1'b1);  // AND_Gate
  and and_6 (and_6_out, ~B_out, C_out, D_out, 1'b1);  // AND_Gate
  or or_1 (or_1_out, and_1_out, and_2_out, and_3_out, 1'b0);
  or or_2 (or_2_out, and_4_out, and_5_out, and_6_out, 1'b0);
  LED B_2 (.in(or_1_out));
  and and_7 (and_7_out, ~or_1_out, ~or_2_out);  // AND_Gate
  LED C_2 (.in(or_2_out));
  LED A_2 (.in(and_7_out));
endmodule
